# Fritzing sketch p56-8 (saved by Fritzing 0.9.4)
breadboards: 1

parts:
  R1 = Rotary Potentiometer (Small) [maximum_resistance=100kΩ package=THT]
  LED1 = LED - 5mm [color="Red (633nm)" package="5 mm [THT]"]
  U1 = ESP32-38PinWide [part_number=ESP32-38PinWide]

nets:
  N1: R1.leg1, U1.GND
  N2: R1.wiper, U1.GPIO25
  N3: R1.leg2, U1.VIN
  N4: LED1.cathode, U1.GPIO11
  N5: LED1.anode, U1.GPIO26

custom parts:
  ESP32-38PinWide: Generic 38-Pin ESP32 with wide format (only access to one side of pins on a breadboard) based on Stephen Lilley's HiLetgo ESP-WROOM-32 ESP32 ESP-32S Development Board.

// code stored in the sketch: homework 20231205.ino
void setup() {
  pinMode(25, INPUT);
  pinMode(26, OUTPUT);
  Serial.begin(9600);
}

double inputVal; // ??????
int outputVal; // ???????
// ??0~4095 ; ??0~255

// ??Pin25(DAC1) ; ??Pin26(DAC2)

void loop() {
  inputVal = analogRead(25);

  outputVal = inputVal / 16;

  
  analogWrite(26, outputVal);

  // ?????
  Serial.print("????: ");
  Serial.print(outputVal);
  Serial.print(" | ??????: ");
  Serial.println(inputVal);

  delay(10);
}

// code stored in the sketch: p56-8.ino
void setup() {
  pinMode(25, INPUT);
  pinMode(26, OUTPUT);
  Serial.begin(9600);
}

double inputVal; // ??????
int outputVal; // ???????
// ??0~4095 ; ??0~255

// ??Pin25(DAC1) ; ??Pin26(DAC2)

void loop() {
  inputVal = analogRead(25);

  outputVal = inputVal / 16;

  
  analogWrite(26, outputVal);

  // ?????
  Serial.print("????: ");
  Serial.print(outputVal);
  Serial.print(" | ??????: ");
  Serial.println(inputVal);

  delay(10);
}
